# Fritzing sketch volt_to_freq_conv-bb (saved by Fritzing 0.9.3b)
breadboards: 1

parts:
  R1 = Resistor [tolerance=±5% resistance=2.2k package=THT]
  U1 = AD654 - Low Cost Monolithic Voltage-to-Frequency Converter [part_number=AD654]
  100pF = Capacitor [package=cap-pth-small2]
  C3 = Ceramic Capacitor [capacitance=4.7nF package="0603 [SMD, multilayer]"]
  R2 = Resistor [tolerance=±5% resistance=10k package=THT]
  R3 = Resistor [tolerance=±5% resistance=4.7k package=THT]
  VCC1 = Battery block 9V

nets:
  N1: R1.Pin_1, U1.10V
  N2: U1.5V, U1.STROBE, C3.1, R2.Pin_1, VCC1.-
  N3: U1.2p5V, R2.Pin_0
  N4: U1.COMMON, C3.0, R3.Pin_0
  N5: U1.VBG, 100pF.2
  N6: U1.CAP, 100pF.1
  N7: U1.V+, VCC1.+

notes:
  1-
  1+
  W1
  GND
  Vp
